// Logisim project ALU.circ as structural Verilog: 1 circuit, main circuit ALU
module ALU (
  input  [31:0] A,
  input  [31:0] B,
  input  [4:0] Shift,
  input  [3:0] Codop,
  input  CarryIn,
  output [31:0] S,
  output [3:0] Flags
);

  wire adder_1_cout, adder_3_cout, and_4_out, and_5_out, and_6_out, bitselector_1_out, bitselector_2_out,
       subtractor_1_bout, subtractor_4_bout, xnor_1_out, xnor_2_out, xor_2_out, xor_3_out, xor_4_out,
       xor_5_out, xor_6_out, xor_7_out;
  wire [4:0] subtractor_5_out, subtractor_6_out, subtractor_7_out;
  wire [31:0] adder_1_out, adder_2_out, adder_3_out, and_1_out, and_2_out, and_3_out, multiplier_1_out,
       not_1_out, not_2_out, or_1_out, shifter_1_out, shifter_2_out, shifter_3_out, shifter_4_out,
       subtractor_1_out, subtractor_2_out, subtractor_3_out, subtractor_4_out, xor_1_out;

  Subtractor #(.width(32)) subtractor_1 (.a(B), .b(A), .out(subtractor_1_out), .bout(subtractor_1_bout));  // open: bin
  Subtractor #(.width(32)) subtractor_2 (.a({32{1'b0}}), .b(32'h1), .out(subtractor_2_out));  // open: bin, bout
  assign not_1_out = ~A;  // NOT_Gate not_1, 32 bits wide
  assign and_1_out = A & B;  // AND_Gate and_1, 32 bits wide
  assign xor_1_out = A ^ B;  // XOR_Gate xor_1, 32 bits wide
  Shifter #(.width(32)) shifter_1 (.in(B), .\dist (Shift), .out(shifter_1_out));
  Shifter #(.shift("lr"), .width(32)) shifter_2 (.in(B), .\dist (Shift), .out(shifter_2_out));
  Shifter #(.shift("ar"), .width(32)) shifter_3 (.in(B), .\dist (Shift), .out(shifter_3_out));
  Adder #(.width(32)) adder_1 (.a(A), .b(B), .out(adder_1_out), .cin(CarryIn), .cout(adder_1_cout));
  Adder #(.width(32)) adder_2 (
    .a(subtractor_1_out), .b(subtractor_2_out), .out(adder_2_out), .cin(CarryIn));  // open: cout
  Shifter #(.shift("rr"), .width(32)) shifter_4 (.in(B), .\dist (Shift), .out(shifter_4_out));
  assign and_2_out = A & B;  // AND_Gate and_2, 32 bits wide
  Subtractor #(.width(32)) subtractor_3 (.a(A), .b({32{1'b0}}), .out(subtractor_3_out));  // open: bin, bout
  Subtractor #(.width(32)) subtractor_4 (.a(B), .b(A), .out(subtractor_4_out), .bout(subtractor_4_bout));  // open: bin
  Adder #(.width(32)) adder_3 (.a(A), .b(B), .out(adder_3_out), .cout(adder_3_cout));  // open: cin
  assign or_1_out = A | B;  // OR_Gate or_1, 32 bits wide
  Multiplier #(.width(32)) multiplier_1 (.a(A), .b(B), .out(multiplier_1_out));  // open: cin, cout
  assign and_3_out = not_1_out & B;  // AND_Gate and_3, 32 bits wide
  assign not_2_out = ~A;  // NOT_Gate not_2, 32 bits wide
  Multiplexer #(.enable("false"), .select(4), .width(32)) multiplexer_1 (
    .in0(and_1_out), .in1(xor_1_out), .in2(shifter_1_out), .in3(shifter_2_out), .in4(shifter_3_out),
    .in5(adder_1_out), .in6(adder_2_out), .in7(shifter_4_out), .in8(and_2_out), .in9(subtractor_3_out),
    .in10(subtractor_4_out), .in11(adder_3_out), .in12(or_1_out), .in13(multiplier_1_out), .in14(and_3_out),
    .in15(not_2_out), .out(S), .sel(Codop));
  BitSelector #(.width(32)) bitselector_1 (.in(B), .out(bitselector_1_out), .sel(subtractor_5_out));
  Subtractor #(.width(5)) subtractor_5 (.a(Shift), .b(5'b00001), .out(subtractor_5_out));  // open: bin, bout
  Comparator #(.width(32)) comparator_1 (.a(S), .b({32{1'b0}}), .eq(Flags[0]), .lt(Flags[1]));  // open: gt
  Subtractor #(.width(5)) subtractor_6 (.a(5'b00101), .b(Shift), .out(subtractor_6_out));  // open: bin, bout
  BitSelector #(.width(32)) bitselector_2 (.in(B), .out(bitselector_2_out), .sel(subtractor_7_out));
  Multiplexer #(.enable("false"), .select(4)) multiplexer_2 (
    .in0(1'b0), .in1(1'b0), .in2(1'b0), .in3(bitselector_2_out), .in4(bitselector_1_out),
    .in5(bitselector_1_out), .in6(adder_1_cout), .in7(subtractor_1_bout), .in8(bitselector_1_out),
    .in9(1'b0), .in10(subtractor_4_bout), .in11(adder_3_cout), .in12(1'b0), .in13(1'b0), .in14(1'b0),
    .in15(1'b0), .out(Flags[2]), .sel(Codop));
  Subtractor #(.width(5)) subtractor_7 (.a(subtractor_6_out), .b(5'b00001), .out(subtractor_7_out));  // open: bin, bout
  xor xor_2 (xor_2_out, B[31], S[31]);
  xnor xnor_1 (xnor_1_out, A[31], B[31]);
  xor xor_3 (xor_3_out, B[31], S[31]);
  xor xor_4 (xor_4_out, A[31], B[31]);
  xor xor_5 (xor_5_out, B[31], subtractor_1_out[31]);
  xnor xnor_2 (xnor_2_out, A[31], B[31]);
  xor xor_6 (xor_6_out, B[31], adder_1_out[31]);
  xor xor_7 (xor_7_out, A[31], B[31]);
  and and_4 (and_4_out, xor_2_out, xnor_1_out);
  and and_5 (and_5_out, xor_3_out, xor_4_out);
  and and_6 (and_6_out, xor_5_out, xnor_2_out);
  and and_7 (and_6_out, xor_6_out, xor_7_out);
  Multiplexer #(.enable("false"), .select(4)) multiplexer_3 (
    .in0(1'b0), .in1(1'b0), .in2(1'b0), .in3(1'b0), .in4(1'b0), .in5(and_4_out), .in6(and_5_out), .in7(1'b0),
    .in8(1'b0), .in9(and_6_out), .in10(and_6_out), .in11(1'b0), .in12(1'b0), .in13(1'b0), .in14(1'b0),
    .in15(1'b0), .out(Flags[3]), .sel(Codop));
endmodule
